// Logisim project dip8.circ as structural Verilog: 14 circuits, main circuit main
module main (
);

  wire and_1_out, aout, BHWR, BLWR, CarryFlag, CHWR, CK1, CK2, CLEAR_out, CLWR, Ctrl___K_out, decoder_1_out0,
       decoder_1_out1, decoder_1_out2, decoder_1_out3, MWR, n74x138_decoder_2_y0, n74x138_decoder_2_y1,
       n74x138_decoder_2_y2, n74x138_decoder_2_y3, n74x138_decoder_2_y4, n74x138_decoder_2_y5,
       n74x138_decoder_2_y6, n74x138_decoder_2_y7, nahwr, nainc, nalu, nalwr, nand_1_out, nBHOE, nBLOE,
       nCHOE, nCLOE, NegFlag, nirwr, nmemrd, nmemwr, nMOE, nmsel, nnext, not_2_out, not_3_out, not_4_out,
       not_13_out, npcinc, npcwr, nregoe, nregwr, nsetflags, nshoe, nsloe, nxoe, nyoe, or_2_out, or_5_out,
       or_6_out, periphsel, ramsel, RESET, romsel, shwr, slwr, Step_Resume_out, tclk, twr, xwr, ywr, ZeroFlag;
  wire [2:0] regsel;
  wire [3:0] counter_1_q, opsel;
  wire [7:0] BH, BL, CH, CL, controlled_buffer_1_out, controlled_buffer_2_out, INST, M, pc_1_addr,
       pc_1_addr_2, reg8lr_1_q, rom_1_data, SH, SL, T, t_q, X, Y;
  wire [15:0] A;
  wire [31:23] rom_2_data;

  Button u_RESET (.out(RESET));
  Button Step_Resume (.out(Step_Resume_out));
  Clock Ctrl___K (.out(Ctrl___K_out));
  // Probe on A
  // Probe on T
  // Probe on M
  // Probe on BH
  // Probe on CH
  // Probe on X
  // Probe on SH
  or or_1 (CK1, Step_Resume_out, Ctrl___K_out);
  // Probe on BL
  // Probe on CL
  // Probe on Y
  // Probe on SL
  not not_1 (CK2, CK1);
  // Probe on controlled_buffer_1_out
  // Probe on {pc_1_addr_2, pc_1_addr}
  TTY tty_1 (.data(controlled_buffer_1_out[6:0]), .clk(CK2), .we(periphsel), .clr(RESET));
  not not_2 (not_2_out, RESET);
  or or_2 (or_2_out, nmemwr, CK1);
  Button CLEAR (.out(CLEAR_out));
  Decoder #(.select(4), .disabled(0), .enable("false")) decoder_1 (
    .out0(decoder_1_out0), .out1(decoder_1_out1), .out2(decoder_1_out2), .out3(decoder_1_out3),
    .out15(periphsel), .sel(pc_1_addr_2[7:4]));  // open: out4, out5, out6, out7, out8, out9, out10, out11, out12, out13, out14
  Counter #(.width(4), .max('hf)) counter_1 (
    .count(1'b1), .Q(counter_1_q), .clk(CK1), .clr(nand_1_out));  // open: load, D, carry
  nand nand_1 (nand_1_out, not_2_out, nnext);
  assign controlled_buffer_1_out = and_1_out ? rom_1_data : 8'bz;  // Controlled_Buffer controlled_buffer_1
  ROM #(.addrWidth(16)) rom_1 (.addr({pc_1_addr_2, pc_1_addr}), .data(rom_1_data), .sel(romsel));
  and and_1 (and_1_out, romsel, not_3_out);
  assign controlled_buffer_2_out = nmemrd ? controlled_buffer_1_out : 8'bz;  // Controlled_Buffer controlled_buffer_2
  RAM #(.addrWidth(16), .bus("asynch")) ram_1 (
    .addr({pc_1_addr_2, pc_1_addr}), .data(controlled_buffer_2_out), .sel(ramsel), .ld(or_2_out),
    .clr(CLEAR_out));
  assign controlled_buffer_1_out = not_3_out ? controlled_buffer_2_out : 8'bz;  // Controlled_Buffer controlled_buffer_3
  not not_3 (not_3_out, nmemrd);
  or or_3 (romsel, decoder_1_out0, decoder_1_out1, decoder_1_out2, decoder_1_out3);
  // Probe on counter_1_q
  // Probe on INST
  not not_4 (not_4_out, nirwr);
  nor nor_1 (ramsel, romsel, periphsel);
  Register register_1 (.D(controlled_buffer_1_out), .en(not_4_out), .Q(INST), .clk(CK1), .clr(RESET));
  _74x138_decoder u_74x138_decoder_1 (
    .G1(nmsel), .nG2A(1'b0), .nG2B(nregoe), .SEL(regsel), .Y0(nBHOE), .Y1(nBLOE), .Y2(nCHOE), .Y3(nCLOE),
    .Y4(nxoe), .Y5(nyoe), .Y6(nshoe), .Y7(nsloe));
  not not_5 (BHWR, n74x138_decoder_2_y0);
  _74x138_decoder u_74x138_decoder_2 (
    .G1(nmsel), .nG2A(CK1), .nG2B(nregwr), .SEL(regsel), .Y0(n74x138_decoder_2_y0),
    .Y1(n74x138_decoder_2_y1), .Y2(n74x138_decoder_2_y2), .Y3(n74x138_decoder_2_y3),
    .Y4(n74x138_decoder_2_y4), .Y5(n74x138_decoder_2_y5), .Y6(n74x138_decoder_2_y6), .Y7(n74x138_decoder_2_y7));
  not not_6 (BLWR, n74x138_decoder_2_y1);
  not not_7 (CHWR, n74x138_decoder_2_y2);
  not not_8 (CLWR, n74x138_decoder_2_y3);
  not not_9 (xwr, n74x138_decoder_2_y4);
  not not_10 (ywr, n74x138_decoder_2_y5);
  not not_11 (shwr, n74x138_decoder_2_y6);
  not not_12 (slwr, n74x138_decoder_2_y7);
  ROM #(.addrWidth(16), .dataWidth(32)) rom_2 (
    .addr({1'b0, NegFlag, ZeroFlag, CarryFlag, INST, counter_1_q}),
    .data({rom_2_data, nmsel, nsetflags, twr, nalu, regsel, opsel, nregwr, nregoe, nalwr, nahwr, nainc, nmemwr, nmemrd, nirwr, npcwr, npcinc, aout, nnext}));  // open: sel
  reg8LR reg8lr_1 (.D(controlled_buffer_1_out), .Rst(RESET), .View(M), .Q(reg8lr_1_q), .Clk(MWR), .nOE(nMOE));
  reg8LR reg8lr_2 (.D(controlled_buffer_1_out), .Rst(RESET), .View(BH), .Q(reg8lr_1_q), .Clk(BHWR), .nOE(nBHOE));
  reg8LR reg8lr_3 (.D(controlled_buffer_1_out), .Rst(RESET), .View(X), .Q(reg8lr_1_q), .Clk(xwr), .nOE(nxoe));
  pc pc_1 (
    .DL(pc_1_addr), .DH(pc_1_addr_2), .Clk(CK1), .Rst(RESET), .nPCNext(npcinc), .nWR(npcwr), .nOE(aout),
    .Addr({pc_1_addr_2, pc_1_addr}));
  reg8LR reg8lr_4 (.D(controlled_buffer_1_out), .Rst(RESET), .View(BL), .Q(reg8lr_1_q), .Clk(BLWR), .nOE(nBLOE));
  reg8LR reg8lr_5 (.D(controlled_buffer_1_out), .Rst(RESET), .View(Y), .Q(reg8lr_1_q), .Clk(ywr), .nOE(nyoe));
  not not_13 (not_13_out, aout);
  _16BitCtrRegister u_16bitctrregister_1 (
    .Clk(CK2), .Rst(RESET), .ninc(nainc), .nLWR(nalwr), .nHWR(nahwr), .noe(not_13_out),
    .DL(controlled_buffer_1_out), .DH(controlled_buffer_1_out), .Addr({pc_1_addr_2, pc_1_addr}), .View(A));
  or or_4 (nMOE, nmsel, nregoe);
  or or_5 (or_5_out, nmsel, nregwr);
  reg8LR reg8lr_6 (.D(controlled_buffer_1_out), .Rst(RESET), .View(CH), .Q(reg8lr_1_q), .Clk(CHWR), .nOE(nCHOE));
  reg8LR reg8lr_7 (.D(controlled_buffer_1_out), .Rst(RESET), .View(SH), .Q(reg8lr_1_q), .Clk(shwr), .nOE(nshoe));
  not not_14 (MWR, or_6_out);
  or or_6 (or_6_out, or_5_out, CK1);
  reg8LR reg8lr_8 (.D(controlled_buffer_1_out), .Rst(RESET), .View(CL), .Q(reg8lr_1_q), .Clk(CLWR), .nOE(nCLOE));
  reg8LR reg8lr_9 (.D(controlled_buffer_1_out), .Rst(RESET), .View(SL), .Q(reg8lr_1_q), .Clk(slwr), .nOE(nsloe));
  reg8LR u_t (.D(controlled_buffer_1_out), .Rst(RESET), .View(T), .Q(t_q), .Clk(tclk), .nOE(1'b0));
  and and_2 (tclk, CK2, twr);
  alu alu_1 (
    .A(reg8lr_1_q), .B(t_q), .opsel(opsel), .nsetflags(nsetflags), .cout(CarryFlag), .z(ZeroFlag),
    .n(NegFlag), .noe(nalu), .reset(RESET), .clk(CK2), .Q(controlled_buffer_1_out));

  // Notes on the sheet:
  //   Debug
  //   Sequencer
  //   contents of rom_1 (hex, n*v repeats v):
  //   6d 0 80 39 0 47 0 20 38 0 e 14 b1 0 6d 3f 0 38 0 17 14 e9 0 0 48 0 20 38 0 21 14 b1 0 6d 43 0 38 0
  //   2a 14 e9 0 0 47 0 24 0 48 0 25 38 0 38 14 49 0 38 0 3e 14 b9 0 ff 3 20 78 20 3 20 3d 20 46 45 5c 0
  //   63 8 71 0 d3 18 55 0 64 70 d0 d3 18 5c 0 64 70 d0 d3 18 63 0 64 70 d0 d3 18 6a 0 64 70 d0 d3 18 71 0
  //   64 70 d0 d3 18 78 0 64 70 d0 d3 18 7f 0 64 70 d0 d3 18 86 0 64 70 d0 d3 44 1e 63 0 66 a4 1c 93 0 67
  //   a6 18 9e 0 67 82 66 98 f1 14 8c 0 a3 0 1c a8 0 a1 0 1a b0 0 5c 1 73 30 0 0 f0 29 1e 40 0 4a 5c 0 14
  //   cd 0 5c 0 6e 10 27 38 0 c4 14 8a 0 6e e8 3 38 0 cd 14 8a 0 6e 64 0 38 0 d6 14 8a 0 6e a 0 38 0 df 14
  //   8a 0 6e 1 0 38 0 e8 14 8a 0 1e 6e 0 f0 1 20 f2 1 21 2 29 f4 1c ee 0 1e
  //   Instruction register
  //   Decoder
  //   Register selection
  //   contents of rom_2 (hex, n*v repeats v):
  //   280fc9 280dd9 280ed9 13*280ffc 280fc9 2109fd 200afd 13*280ffc 280fc9 2309fd 220afd 13*280ffc 280fc9
  //   2709fd 260afd 13*280ffc 280fc9 380fd9 2129fd 209afd 12*280ffc 280fc9 380fd9 2329fd 229afd 12*280ffc
  //   280fc9 380fd9 2729fd 269afd 12*280ffc 280fc9 380fd9 2129fd 380fd9 204afd 11*280ffc 280fc9 380fd9
  //   2329fd 380fd9 224afd 11*280ffc 280fc9 380fd9 2729fd 380fd9 264afd 11*280ffc 280fc9 340bfd 2129fd
  //   209afd 12*280ffc 280fc9 340bfd 2329fd 229afd 12*280ffc 280fc9 340bfd 2729fd 269afd 12*280ffc 280fc9
  //   350bfd 2129fd 209afd 12*280ffc 280fc9 350bfd 2329fd 229afd 12*280ffc 280fc9 350bfd 2729fd 269afd
  //   12*280ffc 280fc9 370bfd 2129fd 360bfd 204afd 11*280ffc 280fc9 370bfd 2329fd 360bfd 224afd 11*280ffc
  //   280fc9 310bfd 2329fd 300bfd 224afd 11*280ffc 280fc9 380f5f 280edf 201dfd 12*280ffc 280fc9 280dd9
  //   280ed9 280ff7 12*280ffc 280fc9 280ff7 14*280ffc 280fc9 280dd9 280ed9 13*280ffc 280fc9 15*280ffc
  //   280fc9 280dd9 280ed9 280ff7 12*280ffc 280fc9 280ff7 14*280ffc 280fc9 280dd9 280ed9 13*280ffc 280fc9
  //   15*280ffc 280fc9 280dd9 280ed9 280ff7 12*280ffc 280fc9 280ff7 14*280ffc 280fc9 27a1fd 2692fd 380fdf
  //   27a1fd 2692fd 280edf 201dfd 280ff7 7*280ffc 280fc9 380fd9 201fbf 13*280ffc 280fc9 2c07df 14*280ffc
  //   280fc9 2d07df 14*280ffc 280fc9 2907df 280f7d 2807df 12*280ffc 280fc9 2b07df 280f7d 2a07df 12*280ffc
  //   280fc9 2807df 14*280ffc 280fc9 2907df 14*280ffc 280fc9 2a07df 14*280ffc 280fc9 2b07df 14*280ffc
  //   280fc9 240bbf 14*280ffc 280fc9 250bbf 14*280ffc 280fc9 210bbf 280f7d 200bbf 12*280ffc 280fc9 230bbf
  //   280f7d 220bbf 12*280ffc 280fc9 200bbf 14*280ffc 280fc9 210bbf 14*280ffc 280fc9 220bbf 14*280ffc
  //   280fc9 230bbf 14*280ffc 280fc9 2709fd 260afd 240bbf 27b3fd 26c3fd 10*280ffc 280fc9 2709fd 260afd
  //   250bbf 27b3fd 26c3fd 10*280ffc 280fc9 2709fd 260afd 200bbf 27b1fd 26c2fd 210bbf 27b3fd 26c3fd
  //   7*280ffc 280fc9 2709fd 260afd 220bbf 27b1fd 26c2fd 230bbf 27b3fd 26c3fd 7*280ffc 280fc9 27a1fd
  //   2692fd 2c07df 12*280ffc 280fc9 27a1fd 2692fd 2d07df 12*280ffc 280fc9 27a1fd 2692fd 2907df 27a1fd
  //   2692fd 2807df 9*280ffc 280fc9 27a1fd 2692fd 2b07df 27a1fd 2692fd 2a07df 9*280ffc 280fc9 380fd9
  //   2709fd 260afd 201fbf 380fd9 27b1fd 26c2fd 201fbf 27b1fd 26c2fd 5*280ffc 280fc9 310bfd 2717fd 300bfd
  //   2617fd 11*280ffc 280fc9 330bfd 2717fd 320bfd 2617fd 11*280ffc 280fc9 370bfd 2117fd 360bfd 2017fd
  //   11*280ffc 280fc9 370bfd 2317fd 360bfd 2217fd 11*280ffc 48*280ffd 280fc9 2807d9 14*280ffc 280fc9
  //   310bfd 2017fd 13*280ffc 280fc9 320bfd 2017fd 13*280ffc 280fc9 330bfd 2017fd 13*280ffc 280fc9 340bfd
  //   2017fd 13*280ffc 280fc9 350bfd 2017fd 13*280ffc 280fc9 300bfd 2117fd 13*280ffc 280fc9 2907d9
  //   14*280ffc 280fc9 320bfd 2117fd 13*280ffc 280fc9 330bfd 2117fd 13*280ffc 280fc9 340bfd 2117fd
  //   13*280ffc 280fc9 350bfd 2117fd 13*280ffc 280fc9 300bfd 2217fd 13*280ffc 280fc9 310bfd 2217fd
  //   13*280ffc 280fc9 2a07d9 14*280ffc 280fc9 330bfd 2217fd 13*280ffc 280fc9 340bfd 2217fd 13*280ffc
  //   280fc9 350bfd 2217fd 13*280ffc 280fc9 300bfd 2317fd 13*280ffc 280fc9 310bfd 2317fd 13*280ffc 280fc9
  //   320bfd 2317fd 13*280ffc 280fc9 2b07d9 14*280ffc 280fc9 340bfd 2317fd 13*280ffc 280fc9 350bfd 2317fd
  //   13*280ffc 280fc9 300bfd 2417fd 13*280ffc 280fc9 310bfd 2417fd 13*280ffc 280fc9 320bfd 2417fd
  //   13*280ffc 280fc9 330bfd 2417fd 13*280ffc 280fc9 2c07d9 14*280ffc 280fc9 350bfd 2417fd 13*280ffc
  //   280fc9 300bfd 2517fd 13*280ffc 280fc9 310bfd 2517fd 13*280ffc 280fc9 320bfd 2517fd 13*280ffc 280fc9
  //   330bfd 2517fd 13*280ffc 280fc9 340bfd 2517fd 13*280ffc 280fc9 2d07d9 14*280ffc 280fc9 300bfd
  //   14*280ffc 280fc9 310bfd 14*280ffc 280fc9 320bfd 14*280ffc 280fc9 330bfd 14*280ffc 280fc9 340bfd
  //   14*280ffc 280fc9 350bfd 14*280ffc 280fc9 380fd9 14*280ffc 280fc9 330bfd 2117fd 320bfd 2017fd
  //   11*280ffc 280fc9 310bfd 2317fd 300bfd 2217fd 11*280ffc 280fc9 2907d9 2807d9 13*280ffc 280fc9 2b07d9
  //   2a07d9 13*280ffc 280fc9 380fdf 14*280ffc 280fc9 423fd 14*280ffc 280fc9 380fd9 423fd 13*280ffc 280fc9
  //   523fd 14*280ffc 280fc9 380fd9 523fd 13*280ffc 280fc9 23fd 14*280ffc 280fc9 380fd9 23fd 13*280ffc
  //   280fc9 123fd 14*280ffc 280fc9 380fd9 123fd 13*280ffc 280fc9 223fd 14*280ffc 280fc9 380fd9 223fd
  //   13*280ffc 280f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
  //   Registers
endmodule

// A
module _16BitCtrRegister (
  input  [7:0] DL,
  input  [7:0] DH,
  input  Clk,
  input  Rst,
  input  ninc,
  input  nLWR,
  input  nHWR,
  input  noe,
  output [15:0] View,
  output [15:0] Addr
);

  wire n74x469_counter_1_ncbo, not_1_out, or_1_out;

  // Probe on DL
  _74x469_counter u_74x469_counter_1 (
    .D(DL), .nUD(1'b0), .nCBI(ninc), .nLD(nLWR), .CK(Clk), .Rst(Rst), .nOE(1'b0),
    .nCBO(n74x469_counter_1_ncbo), .Q(View[7:0]));
  // Probe on DH
  or or_1 (or_1_out, n74x469_counter_1_ncbo, ninc);
  _74x469_counter u_74x469_counter_2 (
    .D(DH), .nUD(1'b0), .nCBI(or_1_out), .nLD(nHWR), .CK(Clk), .Rst(Rst), .nOE(1'b0), .Q(View[15:8]));  // open: nCBO
  // Probe on View
  not not_1 (not_1_out, noe);
  assign Addr = not_1_out ? View : 16'bz;  // Controlled_Buffer controlled_buffer_1
endmodule

module _74x469_counter (
  input  [7:0] D,
  input  nUD,
  input  nCBI,
  input  nLD,
  input  CK,
  input  Rst,
  input  nOE,
  output [7:0] Q,
  output nCBO
);

  wire and_1_out, and_2_out, counter_1_carry, not_1_out, not_2_out, not_3_out, or_1_out;
  wire [7:0] counter_1_q;

  not not_1 (not_1_out, nCBI);
  and and_1 (and_1_out, nUD, not_1_out, nLD);
  not not_2 (not_2_out, nLD);
  or or_1 (or_1_out, and_1_out, not_2_out);
  and and_2 (and_2_out, not_1_out, nLD);
  assign Q = not_3_out ? counter_1_q : 8'bz;  // Controlled_Buffer controlled_buffer_1
  Counter counter_1 (
    .load(or_1_out), .D(D), .count(and_2_out), .Q(counter_1_q), .carry(counter_1_carry), .clk(CK), .clr(Rst));
  not not_3 (not_3_out, nOE);
  not not_4 (nCBO, counter_1_carry);
endmodule

module _74x181_ALU (
  input  [3:0] S,
  input  [3:0] A,
  input  [3:0] B,
  input  M,
  input  Cn,
  output Cn_4,
  output [3:0] F,
  output A_B
);

  wire and_1_out, and_2_out, and_3_out, and_4_out, and_5_out, and_6_out, and_7_out, and_8_out, and_9_out,
       and_10_out, and_11_out, and_12_out, and_13_out, and_14_out, and_15_out, and_16_out, and_17_out,
       and_18_out, and_19_out, and_20_out, and_21_out, and_22_out, and_23_out, and_24_out, and_25_out,
       and_26_out, and_27_out, and_28_out, and_29_out, and_30_out, and_31_out, and_32_out, buffer_1_out,
       buffer_2_out, buffer_3_out, buffer_4_out, buffer_5_out, nand_1_out, nand_2_out, nand_3_out, nor_1_out,
       nor_2_out, nor_3_out, nor_4_out, nor_5_out, nor_6_out, nor_7_out, nor_8_out, nor_9_out, nor_10_out,
       nor_11_out, nor_12_out, not_1_out, not_2_out, not_3_out, not_4_out, not_5_out, not_6_out, not_7_out,
       not_8_out, not_9_out;

  not not_1 (not_1_out, M);
  not not_2 (not_2_out, B[3]);
  not not_3 (not_3_out, B[2]);
  not not_4 (not_4_out, B[1]);
  not not_5 (not_5_out, B[0]);
  and and_1 (and_1_out, B[3], S[3], A[3]);
  and and_2 (and_2_out, A[3], S[2], not_2_out);
  and and_3 (and_3_out, not_2_out, S[1]);
  and and_4 (and_4_out, S[0], B[3]);
  buf buffer_1 (buffer_1_out, A[3]);
  and and_5 (and_5_out, B[2], S[3], A[2]);
  and and_6 (and_6_out, A[2], S[2], not_3_out);
  and and_7 (and_7_out, not_3_out, S[1]);
  and and_8 (and_8_out, S[0], B[2]);
  buf buffer_2 (buffer_2_out, A[2]);
  and and_9 (and_9_out, B[1], S[3], A[1]);
  and and_10 (and_10_out, A[1], S[2], not_4_out);
  and and_11 (and_11_out, not_4_out, S[1]);
  and and_12 (and_12_out, S[0], B[1]);
  buf buffer_3 (buffer_3_out, A[1]);
  and and_13 (and_13_out, B[0], S[3], A[0]);
  and and_14 (and_14_out, A[0], S[2], not_5_out);
  and and_15 (and_15_out, not_5_out, S[1]);
  and and_16 (and_16_out, S[0], B[0]);
  buf buffer_4 (buffer_4_out, A[0]);
  nor nor_1 (nor_1_out, and_1_out, and_2_out);
  nor nor_2 (nor_2_out, and_3_out, and_4_out, buffer_1_out);
  nor nor_3 (nor_3_out, and_5_out, and_6_out);
  nor nor_4 (nor_4_out, and_7_out, and_8_out, buffer_2_out);
  nor nor_5 (nor_5_out, and_9_out, and_10_out);
  nor nor_6 (nor_6_out, and_11_out, and_12_out, buffer_3_out);
  nor nor_7 (nor_7_out, and_13_out, and_14_out);
  nor nor_8 (nor_8_out, and_15_out, and_16_out, buffer_4_out);
  buf buffer_5 (buffer_5_out, nor_2_out);
  and and_17 (and_17_out, nor_1_out, nor_4_out);
  and and_18 (and_18_out, nor_1_out, nor_3_out, nor_6_out);
  and and_19 (and_19_out, nor_1_out, nor_3_out, nor_5_out, nor_8_out);
  nand nand_1 (nand_1_out, nor_1_out, nor_3_out, nor_5_out, nor_7_out, Cn);
  nand nand_2 (nand_2_out, nor_1_out, nor_3_out, nor_5_out, nor_7_out);
  not not_6 (not_6_out, nor_2_out);
  and and_20 (and_20_out, nor_3_out, nor_5_out, nor_7_out, Cn, not_1_out);
  and and_21 (and_21_out, nor_3_out, nor_5_out, nor_8_out, not_1_out);
  and and_22 (and_22_out, nor_3_out, nor_6_out, not_1_out);
  and and_23 (and_23_out, nor_4_out, not_1_out);
  not not_7 (not_7_out, nor_4_out);
  and and_24 (and_24_out, nor_5_out, nor_7_out, Cn, not_1_out);
  and and_25 (and_25_out, nor_5_out, nor_8_out, not_1_out);
  and and_26 (and_26_out, nor_6_out, not_1_out);
  not not_8 (not_8_out, nor_6_out);
  and and_27 (and_27_out, Cn, nor_7_out, not_1_out);
  and and_28 (and_28_out, nor_8_out, not_1_out);
  not not_9 (not_9_out, nor_8_out);
  nand nand_3 (nand_3_out, not_1_out, Cn);
  nor nor_9 (nor_9_out, buffer_5_out, and_17_out, and_18_out, and_19_out);
  and and_29 (and_29_out, nor_1_out, not_6_out);
  nor nor_10 (nor_10_out, and_20_out, and_21_out, and_22_out, and_23_out);
  and and_30 (and_30_out, nor_3_out, not_7_out);
  nor nor_11 (nor_11_out, and_24_out, and_25_out, and_26_out);
  and and_31 (and_31_out, nor_5_out, not_8_out);
  nor nor_12 (nor_12_out, and_27_out, and_28_out);
  and and_32 (and_32_out, nor_7_out, not_9_out);
  or or_1 (Cn_4, ~nor_9_out, ~nand_1_out);  // OR_Gate
  xor xor_1 (F[3], and_29_out, nor_10_out);
  xor xor_2 (F[2], and_30_out, nor_11_out);
  xor xor_3 (F[1], and_31_out, nor_12_out);
  xor xor_4 (F[0], and_32_out, nand_3_out);
  and and_33 (A_B, F[3], F[2], F[1], F[0]);

  // Notes on the sheet:
  //   Carry propagate
  //   Carry generate
endmodule

module _74x138_decoder (
  input  G1,
  input  nG2A,
  input  nG2B,
  input  [2:0] SEL,
  output Y0,
  output Y1,
  output Y2,
  output Y3,
  output Y4,
  output Y5,
  output Y6,
  output Y7
);

  wire and_1_out, decoder_1_out0, decoder_1_out1, decoder_1_out2, decoder_1_out3, decoder_1_out4,
       decoder_1_out5, decoder_1_out6, decoder_1_out7, not_1_out;

  not not_1 (not_1_out, G1);
  and and_1 (and_1_out, ~not_1_out, ~nG2A, ~nG2B);  // AND_Gate
  Decoder #(.select(3), .disabled(0)) decoder_1 (
    .out0(decoder_1_out0), .out1(decoder_1_out1), .out2(decoder_1_out2), .out3(decoder_1_out3),
    .out4(decoder_1_out4), .out5(decoder_1_out5), .out6(decoder_1_out6), .out7(decoder_1_out7), .sel(SEL),
    .en(and_1_out));
  not not_2 (Y0, decoder_1_out0);
  not not_3 (Y2, decoder_1_out2);
  not not_4 (Y4, decoder_1_out4);
  not not_5 (Y6, decoder_1_out6);
  not not_6 (Y1, decoder_1_out1);
  not not_7 (Y3, decoder_1_out3);
  not not_8 (Y5, decoder_1_out5);
  not not_9 (Y7, decoder_1_out7);
endmodule

module RAMController (
  input  [7:0] RAMin,
  input  [7:0] BUSin,
  input  Clk,
  input  nWR,
  input  nOE,
  output nWE,
  output [7:0] RAMout,
  output [7:0] BUSout
);

  wire not_1_out, not_2_out, not_3_out, or_1_out;

  or or_1 (or_1_out, Clk, not_1_out);
  not not_1 (not_1_out, Clk);
  or or_2 (nWE, or_1_out, nWR);
  assign RAMout = not_2_out ? BUSin : 8'bz;  // Controlled_Buffer controlled_buffer_1
  not not_2 (not_2_out, nWR);
  assign BUSout = not_3_out ? RAMin : 8'bz;  // Controlled_Buffer controlled_buffer_2
  not not_3 (not_3_out, nOE);
endmodule

module _74x374_ff (
  input  [7:0] D,
  input  Clk,
  input  Rst,
  input  nOC,
  output [7:0] View,
  output [7:0] Q
);

  wire not_1_out;

  Register register_1 (.D(D), .en(1'b1), .Q(View), .clk(Clk), .clr(Rst));
  assign Q = not_1_out ? View : 8'bz;  // Controlled_Buffer controlled_buffer_1
  not not_1 (not_1_out, nOC);
endmodule

module _74x139 (
  input  E,
  input  [1:0] SEL,
  output Y0,
  output Y1,
  output Y2,
  output Y3
);

  wire decoder_1_out0, decoder_1_out1, decoder_1_out2, decoder_1_out3, not_1_out;

  not not_1 (not_1_out, E);
  Decoder #(.select(2), .disabled(0)) decoder_1 (
    .out0(decoder_1_out0), .out1(decoder_1_out1), .out2(decoder_1_out2), .out3(decoder_1_out3), .sel(SEL),
    .en(not_1_out));
  not not_2 (Y0, decoder_1_out0);
  not not_3 (Y2, decoder_1_out2);
  not not_4 (Y1, decoder_1_out1);
  not not_5 (Y3, decoder_1_out3);
endmodule

module _74x157 (
  input  [3:0] A,
  input  [3:0] B,
  input  Select,
  input  Strobe,
  output [3:0] out
);

  wire not_1_out;

  Multiplexer #(.width(4), .disabled(0)) multiplexer_1 (.in0(A), .in1(B), .out(out), .sel(Select), .en(not_1_out));
  not not_1 (not_1_out, Strobe);
endmodule

module _74x541_buffer (
  input  [7:0] D,
  input  nOE,
  output [7:0] Q
);

  wire not_1_out;

  assign Q = not_1_out ? D : 8'bz;  // Controlled_Buffer controlled_buffer_1
  not not_1 (not_1_out, nOE);
endmodule

module reg8LR (
  input  [7:0] D,
  input  Clk,
  input  Rst,
  input  nOE,
  output [7:0] View,
  output [7:0] Q
);

  _74x374_ff u_74x374_ff_1 (.View(View), .D(D), .Q(Q), .Clk(Clk), .Rst(Rst), .nOC(nOE));
endmodule

// PC
module pc (
  input  [7:0] DL,
  input  [7:0] DH,
  input  Clk,
  input  Rst,
  input  nPCNext,
  input  nWR,
  input  nOE,
  output [15:0] Addr
);

  wire and_1_out, and_2_out, counter_1_carry, not_1_out, not_2_out, not_3_out;
  wire [7:0] counter_1_q, counter_2_q;

  and and_1 (and_1_out, nWR, not_2_out);
  not not_1 (not_1_out, nWR);
  not not_2 (not_2_out, nPCNext);
  Counter counter_1 (
    .load(not_1_out), .D(DL), .count(and_1_out), .Q(counter_1_q), .carry(counter_1_carry), .clk(Clk),
    .clr(Rst));
  and and_2 (and_2_out, counter_1_carry, and_1_out);
  Counter counter_2 (
    .load(not_1_out), .D(DH), .count(and_2_out), .Q(counter_2_q), .clk(Clk), .clr(Rst));  // open: carry
  not not_3 (not_3_out, nOE);
  assign Addr = not_3_out ? {counter_2_q, counter_1_q} : 16'bz;  // Controlled_Buffer controlled_buffer_1
endmodule

// ALU
module alu (
  input  nsetflags,
  input  [3:0] opsel,
  input  noe,
  input  reset,
  input  clk,
  input  [7:0] A,
  input  [7:0] B,
  output cout,
  output z,
  output n,
  output [7:0] Q
);

  wire and_1_out, not_1_out;
  wire [7:0] rom_1_data, rom_2_data;
  wire [13:13] ffwithenable_1_q;

  Pull_Resistor pull_resistor_1 (.node(A));
  ROM #(.addrWidth(16)) rom_1 (
    .addr({1'b0, cout, ffwithenable_1_q[13], opsel, nsetflags, B[3:0], A[3:0]}), .data(rom_1_data), .sel(1'b1));
  ROM #(.addrWidth(16)) rom_2 (
    .addr({1'b1, {2{rom_1_data[4]}}, opsel, nsetflags, B[7:4], A[7:4]}), .data(rom_2_data), .sel(1'b1));
  and and_1 (and_1_out, rom_1_data[5], rom_2_data[5]);
  not not_1 (not_1_out, noe);
  assign Q = not_1_out ? {rom_2_data[3:0], rom_1_data[3:0]} : 8'bz;  // Controlled_Buffer controlled_buffer_1
  FFwithEnable ffwithenable_1 (
    .D(rom_2_data[4]), .nen(rom_1_data[7]), .Clk(clk), .Rst(reset), .Q(ffwithenable_1_q[13]));
  FFwithEnable ffwithenable_2 (.D(rom_2_data[4]), .nen(rom_2_data[7]), .Clk(clk), .Rst(reset), .Q(cout));
  FFwithEnable ffwithenable_3 (.D(and_1_out), .nen(rom_2_data[7]), .Clk(clk), .Rst(reset), .Q(z));
  FFwithEnable ffwithenable_4 (.D(rom_2_data[6]), .nen(rom_2_data[7]), .Clk(clk), .Rst(reset), .Q(n));

  // Notes on the sheet:
  //   LOW
  //   contents of rom_1 (hex, n*v repeats v):
  //   a0 81 82 83 84 85 86 87 c8 c9 ca cb cc cd ce cf a0 81 82 83 84 85 86 87 c8 c9 ca cb cc cd ce cf a0
  //   81 82 83 84 85 86 87 c8 c9 ca cb cc cd ce cf a0 81 82 83 84 85 86 87 c8 c9 ca cb cc cd ce cf a0 81
  //   82 83 84 85 86 87 c8 c9 ca cb cc cd ce cf a0 81 82 83 84 85 86 87 c8 c9 ca cb cc cd ce cf a0 81 82
  //   83 84 85 86 87 c8 c9 ca cb cc cd ce cf a0 81 82 83 84 85 86 87 c8 c9 ca cb cc cd ce cf a0 81 82 83
  //   84 85 86 87 c8 c9 ca cb cc cd ce cf a0 81 82 83 84 85 86 87 c8 c9 ca cb cc cd ce cf a0 81 82 83 84
  //   85 86 87 c8 c9 ca cb cc cd ce cf a0 81 82 83 84 85 86 87 c8 c9 ca cb cc cd ce cf a0 81 82 83 84 85
  //   86 87 c8 c9 ca cb cc cd ce cf a0 81 82 83 84 85 86 87 c8 c9 ca cb cc cd ce cf a0 81 82 83 84 85 86
  //   87 c8 c9 ca cb cc cd ce cf a0 81 82 83 84 85 86 87 c8 c9 ca cb cc cd ce cf a0 81 82 83 84 85 86 87
  //   c8 c9 ca cb cc cd ce cf a0 81 82 83 84 85 86 87 c8 c9 ca cb cc cd ce cf a0 81 82 83 84 85 86 87 c8
  //   c9 ca cb cc cd ce cf a0 81 82 83 84 85 86 87 c8 c9 ca cb cc cd ce cf a0 81 82 83 84 85 86 87 c8 c9
  //   ca cb cc cd ce cf a0 81 82 83 84 85 86 87 c8 c9 ca cb cc cd ce cf a0 81 82 83 84 85 86 87 c8 c9 ca
  //   cb cc cd ce cf a0 81 82 83 84 85 86 87 c8 c9 ca cb cc cd ce cf a0 81 82 83 84 85 86 87 c8 c9 ca cb
  //   cc cd ce cf a0 81 82 83 84 85 86 87 c8 c9 ca cb cc cd ce cf a0 81 82 83 84 85 86 87 c8 c9 ca cb cc
  //   cd ce cf a0 81 82 83 84 85 86 87 c8 c9 ca cb cc cd ce cf a0 81 82 83 84 85 86 87 c8 c9 ca cb cc cd
  //   ce cf a0 81 82 83 84 85 86 87 c8 c9 ca cb cc cd ce cf a0 81 82 83 84 85 86 87 c8 c9 ca cb cc cd ce
  //   cf a0 81 82 83 84 85 86 87 c8 c9 ca cb cc cd ce cf 16*a0 16*81 16*82 16*83 16*84 16*85 16*86 16*87
  //   16*c8 16*c9 16*ca 16*cb 16*cc 16*cd 16*ce 16*cf 16*a0 16*81 16*82 16*83 16*84 16*85 16*86 16*87
  //   16*c8 16*c9 16*ca 16*cb 16*cc 16*cd 16*ce 16*cf a0 81 82 83 84 85 86 87 c8 c9 ca cb cc cd ce cf 81
  //   82 83 84 85 86 87 c8 c9 ca cb cc cd ce cf b0 82 83 84 85 86 87 c8 c9 ca cb cc cd ce cf b0 91 83 84
  //   85 86 87 c8 c9 ca cb cc cd ce cf b0 91 92 84 85 86 87 c8 c9 ca cb cc cd ce cf b0 91 92 93 85 86 87
  //   c8 c9 ca cb cc cd ce cf b0 91 92 93 94 86 87 c8 c9 ca cb cc cd ce cf b0 91 92 93 94 95 87 c8 c9 ca
  //   cb cc cd ce cf b0 91 92 93 94 95 96 c8 c9 ca cb cc cd ce cf b0 91 92 93 94 95 96 97 c9 ca cb cc cd
  //   ce cf b0 91 92 93 94 95 96 97 d8 ca cb cc cd ce cf b0 91 92 93 94 95 96 97 d8 d9 cb cc cd ce cf b0
  //   91 92 93 94 95 96 97 d8 d9 da cc cd ce cf b0 91 92 93 94 95 96 97 d8 d9 da db cd ce cf b0 91 92 93
  //   94 95 96 97 d8 d9 da db dc ce cf b0 91 92 93 94 95 96 97 d8 d9 da db dc dd cf b0 91 92 93 94 95 96
  //   97 d8 d9 da db dc dd de 20 1 2 3 4 5 6 7 48 49 4a 4b 4c 4d 4e 4f 1 2 3 4 5 6 7 48 49 4a 4b 4c 4d 4e
  //   4f 30 2 3 4 5 6 7 48 49 4a 4b 4c 4d 4e 4f 30 11 3 4 5 6 7 48 49 4a 4b 4c 4d 4e 4f 30 11 12 4 5 6 7
  //   48 49 4a 4b 4c 4d 4e 4f 30 11 12 13 5 6 7 48 49 4a 4b 4c 4d 4e 4f 30 11 12 13 14 6 7 48 49 4a 4b 4c
  //   4d 4e 4f 30 11 12 13 14 15 7 48 49 4a 4b 4c 4d 4e 4f 30 11 12 13 14 15 16 48 49 4a 4b 4c 4d 4e 4f 30
  //   11 12 13 14 15 16 17 49 4a 4b 4c 4d 4e 4f 30 11 12 13 14 15 16 17 58 4a 4b 4c 4d 4e 4f 30 11 12 13
  //   14 15 16 17 58 59 4b 4c 4d 4e 4f 30 11 12 13 14 15 16 17 58 59 5a 4c 4d 4e 4f 30 11 12 13 14 15 16
  //   17 58 59 5a 5b 4d 4e 4f 30 11 12 13 14 15 16 17 58 59 5a 5b 5c 4e 4f 30 11 12 13 14 15 16 17 58 59
  //   5a 5b 5c 5d 4f 30 11 12 13 14 15 16 17 58 59 5a 5b 5c 5d 5e b0 91 92 93 94 95 96 97 d8 d9 da db dc
  //   dd de df cf b0 91 92 93 94 95 96 97 d8 d9 da db dc dd de ce cf b0 91 92 93 94 95 96 97 d8 d9 da db
  //   dc dd cd ce cf b0 91 92 93 94 95 96 97 d8 d9 da db dc cc cd ce cf b0 91 92 93 94 95 96 97 d8 d9 da
  //   db cb cc cd ce cf b0 91 92 93 94 95 96 97 d8 d9 da ca cb cc cd ce cf b0 91 92 93 94 95 96 97 d8 d9
  //   c9 ca cb cc cd ce cf b0 91 92 93 94 95 96 97 d8 c8 c9 ca cb cc cd ce cf b0 91 92 93 94 95 96 97 87
  //   c8 c9 ca cb cc cd ce cf b0 91 92 93 94 95 96 86 87 c8 c9 ca cb cc cd ce cf b0 91 92 93 94 95 85 86
  //   87 c8 c9 ca cb cc cd ce cf b0 91 92 93 94 84 85 86 87 c8 c9 ca cb cc cd ce cf b0 91 92 93 83 84 85
  //   86 87 c8 c9 ca cb cc cd ce cf b0 91 92 82 83 84 85 86 87 c8 c9 ca cb cc cd ce cf b0 91 81 82 83 84
  //   85 86 87 c8 c9 ca cb cc cd ce cf b0 30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
  //   HIGH
  //   contents of rom_2 (hex, n*v repeats v):
  //   a0 81 82 83 84 85 86 87 c8 c9 ca cb cc cd ce cf a0 81 82 83 84 85 86 87 c8 c9 ca cb cc cd ce cf a0
  //   81 82 83 84 85 86 87 c8 c9 ca cb cc cd ce cf a0 81 82 83 84 85 86 87 c8 c9 ca cb cc cd ce cf a0 81
  //   82 83 84 85 86 87 c8 c9 ca cb cc cd ce cf a0 81 82 83 84 85 86 87 c8 c9 ca cb cc cd ce cf a0 81 82
  //   83 84 85 86 87 c8 c9 ca cb cc cd ce cf a0 81 82 83 84 85 86 87 c8 c9 ca cb cc cd ce cf a0 81 82 83
  //   84 85 86 87 c8 c9 ca cb cc cd ce cf a0 81 82 83 84 85 86 87 c8 c9 ca cb cc cd ce cf a0 81 82 83 84
  //   85 86 87 c8 c9 ca cb cc cd ce cf a0 81 82 83 84 85 86 87 c8 c9 ca cb cc cd ce cf a0 81 82 83 84 85
  //   86 87 c8 c9 ca cb cc cd ce cf a0 81 82 83 84 85 86 87 c8 c9 ca cb cc cd ce cf a0 81 82 83 84 85 86
  //   87 c8 c9 ca cb cc cd ce cf a0 81 82 83 84 85 86 87 c8 c9 ca cb cc cd ce cf a0 81 82 83 84 85 86 87
  //   c8 c9 ca cb cc cd ce cf a0 81 82 83 84 85 86 87 c8 c9 ca cb cc cd ce cf a0 81 82 83 84 85 86 87 c8
  //   c9 ca cb cc cd ce cf a0 81 82 83 84 85 86 87 c8 c9 ca cb cc cd ce cf a0 81 82 83 84 85 86 87 c8 c9
  //   ca cb cc cd ce cf a0 81 82 83 84 85 86 87 c8 c9 ca cb cc cd ce cf a0 81 82 83 84 85 86 87 c8 c9 ca
  //   cb cc cd ce cf a0 81 82 83 84 85 86 87 c8 c9 ca cb cc cd ce cf a0 81 82 83 84 85 86 87 c8 c9 ca cb
  //   cc cd ce cf a0 81 82 83 84 85 86 87 c8 c9 ca cb cc cd ce cf a0 81 82 83 84 85 86 87 c8 c9 ca cb cc
  //   cd ce cf a0 81 82 83 84 85 86 87 c8 c9 ca cb cc cd ce cf a0 81 82 83 84 85 86 87 c8 c9 ca cb cc cd
  //   ce cf a0 81 82 83 84 85 86 87 c8 c9 ca cb cc cd ce cf a0 81 82 83 84 85 86 87 c8 c9 ca cb cc cd ce
  //   cf a0 81 82 83 84 85 86 87 c8 c9 ca cb cc cd ce cf 16*a0 16*81 16*82 16*83 16*84 16*85 16*86 16*87
  //   16*c8 16*c9 16*ca 16*cb 16*cc 16*cd 16*ce 16*cf 16*a0 16*81 16*82 16*83 16*84 16*85 16*86 16*87
  //   16*c8 16*c9 16*ca 16*cb 16*cc 16*cd 16*ce 16*cf a0 81 82 83 84 85 86 87 c8 c9 ca cb cc cd ce cf 81
  //   82 83 84 85 86 87 c8 c9 ca cb cc cd ce cf b0 82 83 84 85 86 87 c8 c9 ca cb cc cd ce cf b0 91 83 84
  //   85 86 87 c8 c9 ca cb cc cd ce cf b0 91 92 84 85 86 87 c8 c9 ca cb cc cd ce cf b0 91 92 93 85 86 87
  //   c8 c9 ca cb cc cd ce cf b0 91 92 93 94 86 87 c8 c9 ca cb cc cd ce cf b0 91 92 93 94 95 87 c8 c9 ca
  //   cb cc cd ce cf b0 91 92 93 94 95 96 c8 c9 ca cb cc cd ce cf b0 91 92 93 94 95 96 97 c9 ca cb cc cd
  //   ce cf b0 91 92 93 94 95 96 97 d8 ca cb cc cd ce cf b0 91 92 93 94 95 96 97 d8 d9 cb cc cd ce cf b0
  //   91 92 93 94 95 96 97 d8 d9 da cc cd ce cf b0 91 92 93 94 95 96 97 d8 d9 da db cd ce cf b0 91 92 93
  //   94 95 96 97 d8 d9 da db dc ce cf b0 91 92 93 94 95 96 97 d8 d9 da db dc dd cf b0 91 92 93 94 95 96
  //   97 d8 d9 da db dc dd de 20 1 2 3 4 5 6 7 48 49 4a 4b 4c 4d 4e 4f 1 2 3 4 5 6 7 48 49 4a 4b 4c 4d 4e
  //   4f 30 2 3 4 5 6 7 48 49 4a 4b 4c 4d 4e 4f 30 11 3 4 5 6 7 48 49 4a 4b 4c 4d 4e 4f 30 11 12 4 5 6 7
  //   48 49 4a 4b 4c 4d 4e 4f 30 11 12 13 5 6 7 48 49 4a 4b 4c 4d 4e 4f 30 11 12 13 14 6 7 48 49 4a 4b 4c
  //   4d 4e 4f 30 11 12 13 14 15 7 48 49 4a 4b 4c 4d 4e 4f 30 11 12 13 14 15 16 48 49 4a 4b 4c 4d 4e 4f 30
  //   11 12 13 14 15 16 17 49 4a 4b 4c 4d 4e 4f 30 11 12 13 14 15 16 17 58 4a 4b 4c 4d 4e 4f 30 11 12 13
  //   14 15 16 17 58 59 4b 4c 4d 4e 4f 30 11 12 13 14 15 16 17 58 59 5a 4c 4d 4e 4f 30 11 12 13 14 15 16
  //   17 58 59 5a 5b 4d 4e 4f 30 11 12 13 14 15 16 17 58 59 5a 5b 5c 4e 4f 30 11 12 13 14 15 16 17 58 59
  //   5a 5b 5c 5d 4f 30 11 12 13 14 15 16 17 58 59 5a 5b 5c 5d 5e b0 91 92 93 94 95 96 97 d8 d9 da db dc
  //   dd de df cf b0 91 92 93 94 95 96 97 d8 d9 da db dc dd de ce cf b0 91 92 93 94 95 96 97 d8 d9 da db
  //   dc dd cd ce cf b0 91 92 93 94 95 96 97 d8 d9 da db dc cc cd ce cf b0 91 92 93 94 95 96 97 d8 d9 da
  //   db cb cc cd ce cf b0 91 92 93 94 95 96 97 d8 d9 da ca cb cc cd ce cf b0 91 92 93 94 95 96 97 d8 d9
  //   c9 ca cb cc cd ce cf b0 91 92 93 94 95 96 97 d8 c8 c9 ca cb cc cd ce cf b0 91 92 93 94 95 96 97 87
  //   c8 c9 ca cb cc cd ce cf b0 91 92 93 94 95 96 86 87 c8 c9 ca cb cc cd ce cf b0 91 92 93 94 95 85 86
  //   87 c8 c9 ca cb cc cd ce cf b0 91 92 93 94 84 85 86 87 c8 c9 ca cb cc cd ce cf b0 91 92 93 83 84 85
  //   86 87 c8 c9 ca cb cc cd ce cf b0 91 92 82 83 84 85 86 87 c8 c9 ca cb cc cd ce cf b0 91 81 82 83 84
  //   85 86 87 c8 c9 ca cb cc cd ce cf b0 30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
endmodule

module FFwithEnable (
  input  D,
  input  nen,
  input  Clk,
  input  Rst,
  output Q
);

  wire not_1_out;

  not not_1 (not_1_out, nen);
  D_Flip_Flop d_ff_1 (.clk(Clk), .D(D), .Q(Q), .en(not_1_out), .reset(Rst));  // open: Qn, preset
endmodule
